# Fritzing sketch Wiring Diagram (saved by Fritzing 0.9.10b)
breadboards: 5

parts:
  PmodDA1 = PmodDA4
  YwRobot_Power_Supply1 = YwRobot Breadboard Power Supply [part_number=545043]
  R1 = Resistor [tolerance=±5% power=0.25 resistance=220 package=THT]
  Basys_1 = Digilent Basys 3 [part_number=XC7A35T-1CPG236C]
  D1 = Rectifier Diode [part_number=1N4001 package="300 mil [THT]"]
  U2 = 2.5mm Audio Jack [package=stereojack2.5mm_smd]
  IC1 = IC, DIP package, 8 pins [chip_label=6N137]
  R2 = Resistor [tolerance=±5% power=0.25 resistance=220 package=THT]
  R100 = Resistor [tolerance=±5% power=0.25 resistance=1k package=THT]
  R106 = Resistor [tolerance=±5% power=0.25 resistance=1k package=THT]
  IC5 = IC, DIP package, 14 pins [chip_label=LM324N]
  IC6 = IC, DIP package, 8 pins [chip_label=AD835]
  IC7 = IC, DIP package, 16 pins [chip_label=" SSI2144"]
  J1 = Power Jack [package=power_jack_pth_lock]  # not connected
  U27 = XR2206 [package=dil16]
  R115 = Resistor [tolerance=±5% resistance=200 package="0603 [SMD]"]
  C17 = Ceramic Capacitor [capacitance=1µF voltage=35V package="100 mil [THT, multilayer]"]
  R116 = Resistor [tolerance=±5% power=0.25 resistance=50k package=THT]
  C18 = Ceramic Capacitor [capacitance=0.04µF voltage=35V package="100 mil [THT, multilayer]"]
  R117 = Resistor [tolerance=±5% power=0.25 resistance=2912.62 package=THT]
  R118 = Resistor [tolerance=±5% power=0.25 resistance=2040.82 package=THT]
  IC10 = IC, DIP package, 14 pins [chip_label=LM324N]
  R125 = Resistor [tolerance=±5% power=0.25 resistance=1k package=THT]
  R126 = Resistor [tolerance=±5% power=0.25 resistance=1k package=THT]
  R127 = Resistor [tolerance=±5% power=0.25 resistance=1k package=THT]
  R128 = Resistor [tolerance=±5% power=0.25 resistance=1k package=THT]
  R129 = Resistor [tolerance=±5% power=0.25 resistance=1k package=THT]
  R130 = Resistor [tolerance=±5% power=0.25 resistance=1k package=THT]
  U29 = XR2206 [package=dil16]
  R135 = Resistor [tolerance=±5% resistance=200 package="0603 [SMD]"]
  C21 = Ceramic Capacitor [capacitance=1µF voltage=35V package="100 mil [THT, multilayer]"]
  R136 = Resistor [tolerance=±5% power=0.25 resistance=50k package=THT]
  C22 = Ceramic Capacitor [capacitance=0.04µF voltage=35V package="100 mil [THT, multilayer]"]
  R137 = Resistor [tolerance=±5% power=0.25 resistance=2912.62 package=THT]
  R138 = Resistor [tolerance=±5% power=0.25 resistance=2040.82 package=THT]
  U30 = XR2206 [package=dil16]
  R139 = Resistor [tolerance=±5% resistance=200 package="0603 [SMD]"]
  C23 = Ceramic Capacitor [capacitance=1µF voltage=35V package="100 mil [THT, multilayer]"]
  R140 = Resistor [tolerance=±5% power=0.25 resistance=50k package=THT]
  C24 = Ceramic Capacitor [capacitance=0.04µF voltage=35V package="100 mil [THT, multilayer]"]
  R141 = Resistor [tolerance=±5% power=0.25 resistance=2912.62 package=THT]
  R142 = Resistor [tolerance=±5% power=0.25 resistance=2040.82 package=THT]
  U31 = XR2206 [package=dil16]
  U32 = XR2206 [package=dil16]
  U33 = XR2206 [package=dil16]
  R143 = Resistor [tolerance=±5% resistance=200 package="0603 [SMD]"]
  R144 = Resistor [tolerance=±5% resistance=200 package="0603 [SMD]"]
  R145 = Resistor [tolerance=±5% resistance=200 package="0603 [SMD]"]
  C25 = Ceramic Capacitor [capacitance=1µF voltage=35V package="100 mil [THT, multilayer]"]
  C26 = Ceramic Capacitor [capacitance=1µF voltage=35V package="100 mil [THT, multilayer]"]
  C27 = Ceramic Capacitor [capacitance=1µF voltage=35V package="100 mil [THT, multilayer]"]
  R146 = Resistor [tolerance=±5% power=0.25 resistance=50k package=THT]
  R147 = Resistor [tolerance=±5% power=0.25 resistance=50k package=THT]
  R148 = Resistor [tolerance=±5% power=0.25 resistance=50k package=THT]
  C28 = Ceramic Capacitor [capacitance=0.04µF voltage=35V package="100 mil [THT, multilayer]"]
  C29 = Ceramic Capacitor [capacitance=0.04µF voltage=35V package="100 mil [THT, multilayer]"]
  C30 = Ceramic Capacitor [capacitance=0.04µF voltage=35V package="100 mil [THT, multilayer]"]
  R149 = Resistor [tolerance=±5% power=0.25 resistance=2912.62 package=THT]
  R150 = Resistor [tolerance=±5% power=0.25 resistance=2912.62 package=THT]
  R151 = Resistor [tolerance=±5% power=0.25 resistance=2912.62 package=THT]
  R152 = Resistor [tolerance=±5% power=0.25 resistance=2040.82 package=THT]
  R153 = Resistor [tolerance=±5% power=0.25 resistance=2040.82 package=THT]
  R154 = Resistor [tolerance=±5% power=0.25 resistance=2040.82 package=THT]
  IC11 = IC, DIP package, 14 pins [chip_label=LM324N]
  R155 = Resistor [tolerance=±5% power=0.25 resistance=1k package=THT]
  R156 = Resistor [tolerance=±5% power=0.25 resistance=1k package=THT]
  R157 = Resistor [tolerance=±5% power=0.25 resistance=1k package=THT]
  R158 = Resistor [tolerance=±5% power=0.25 resistance=1k package=THT]
  R159 = Resistor [tolerance=±5% power=0.25 resistance=1k package=THT]
  R160 = Resistor [tolerance=±5% power=0.25 resistance=1k package=THT]
  U34 = POT [knob_status=50% power=0.5W package=alps_pot]
  U35 = POT [knob_status=50% power=0.5W package=alps_pot]
  R161 = Resistor [tolerance=±5% power=0.25 resistance=1k package=THT]
  R162 = Resistor [tolerance=±5% power=0.25 resistance=1k package=THT]
  U36 = POT [knob_status=50% power=0.5W package=alps_pot]
  SPKR1 = Loudspeaker

nets:
  N1: PmodDA1.VOUTA, IC10.pin5
  N2: PmodDA1.VOUTC, IC10.pin3
  N3: PmodDA1.VOUTE, IC10.pin12
  GND: PmodDA1.GND, R100.Pin_1, IC5.pin11, IC6.pin3, IC7.pin8, U27.GND, C17.1, R117.Pin_0, IC10.pin11, R125.Pin_0, R127.Pin_0, U29.GND, C21.1, R137.Pin_0, U30.GND, C23.1, R141.Pin_0, U31.GND, U32.GND, U33.GND, C25.1, C26.1, C27.1, R149.Pin_0, R150.Pin_0, R151.Pin_0, IC11.pin11, R155.Pin_0, R157.Pin_0
  N4: PmodDA1.VOUTB, IC11.pin12
  N5: PmodDA1.VOUTD, IC11.pin3
  N6: PmodDA1.VOUTF, IC11.pin5
  N7: YwRobot_Power_Supply1.VCC#5, YwRobot_Power_Supply1.VCC#6
  N8: YwRobot_Power_Supply1.VCC#9, YwRobot_Power_Supply1.VCC#10, Basys_1.5v, IC1.pin7, IC1.pin8
  N9: YwRobot_Power_Supply1.GND#11, YwRobot_Power_Supply1.GND#12
  N10: YwRobot_Power_Supply1.GND#13, YwRobot_Power_Supply1.GND#14, Basys_1.GND, IC1.pin5
  N11: R1.Pin_0, U2.RIGHT
  N12: R1.Pin_1, D1.cathode, IC1.pin2
  N13: Basys_1.JA7, IC1.pin6, R2.Pin_0
  N14: Basys_1.3v3, R2.Pin_1
  N15: Basys_1.JXADC1, IC7.pin2, IC7.pin9, R116.Pin_0, R136.Pin_0, R140.Pin_0, R146.Pin_0, R147.Pin_0, R148.Pin_0, U34.A, U35.E, R161.Pin_1, R162.Pin_1, U36.A, SPKR1.pin2
  N16: Basys_1.JXADC2, U33.STO, U36.E
  N17: Basys_1.JXADC7, Basys_1.JXADC8, IC7.pin3, SPKR1.pin1
  N18: D1.anode, U2.LEFT, IC1.pin3
  N19: R100.Pin_0, R106.Pin_0, IC5.pin6
  N20: R106.Pin_1, IC5.pin7, U27.STO, U29.STO, U31.STO, U32.STO
  VCC: IC5.pin4, IC6.pin6, IC7.pin16, U27.VCC, IC10.pin4, R126.Pin_1, U29.VCC, U30.VCC, U31.VCC, U32.VCC, U33.VCC, IC11.pin4, R156.Pin_1
  N21: IC5.pin5, U34.E
  N22: IC6.pin1, U35.S
  N23: IC6.pin2, R162.Pin_0
  N24: IC6.pin4, U36.S
  N25: IC6.pin5, IC7.pin1
  N26: IC6.pin7, R161.Pin_0
  N27: IC6.pin8, U34.S
  N28: U27.MO, R116.Pin_1
  N29: U27.TC1, C18.1
  N30: U27.TC2, C18.0
  N31: U27.TR1, R117.Pin_1, R118.Pin_0
  N32: U27.BIAS, C17.0
  N33: U27.WAVEA1, R115.Pin_1
  N34: U27.WAVEA2, R115.Pin_0
  N35: R118.Pin_1, IC10.pin7, R130.Pin_1
  N36: IC10.pin1, R128.Pin_0, R142.Pin_1
  N37: IC10.pin2, R127.Pin_1, R128.Pin_1
  N38: IC10.pin6, R125.Pin_1, R130.Pin_0
  N39: IC10.pin13, R126.Pin_0, R129.Pin_1
  N40: IC10.pin14, R129.Pin_0, R138.Pin_1
  N41: U29.MO, R136.Pin_1
  N42: U29.TC1, C22.1
  N43: U29.TC2, C22.0
  N44: U29.TR1, R137.Pin_1, R138.Pin_0
  N45: U29.BIAS, C21.0
  N46: U29.WAVEA1, R135.Pin_1
  N47: U29.WAVEA2, R135.Pin_0
  N48: U30.STO, U35.A
  N49: U30.MO, R140.Pin_1
  N50: U30.TC1, C24.1
  N51: U30.TC2, C24.0
  N52: U30.TR1, R141.Pin_1, R142.Pin_0
  N53: U30.BIAS, C23.0
  N54: U30.WAVEA1, R139.Pin_1
  N55: U30.WAVEA2, R139.Pin_0
  N56: U31.MO, R148.Pin_1
  N57: U31.TC1, C30.1
  N58: U31.TC2, C30.0
  N59: U31.TR1, R150.Pin_1, R154.Pin_0
  N60: U31.BIAS, C27.0
  N61: U31.WAVEA1, R145.Pin_1
  N62: U31.WAVEA2, R145.Pin_0
  N63: U32.MO, R147.Pin_1
  N64: U32.TC1, C28.1
  N65: U32.TC2, C28.0
  N66: U32.TR1, R151.Pin_1, R152.Pin_0
  N67: U32.BIAS, C25.0
  N68: U32.WAVEA1, R144.Pin_1
  N69: U32.WAVEA2, R144.Pin_0
  N70: U33.MO, R146.Pin_1
  N71: U33.TC1, C29.1
  N72: U33.TC2, C29.0
  N73: U33.TR1, R149.Pin_1, R153.Pin_0
  N74: U33.BIAS, C26.0
  N75: U33.WAVEA1, R143.Pin_1
  N76: U33.WAVEA2, R143.Pin_0
  N77: R152.Pin_1, IC11.pin7, R160.Pin_1
  N78: R153.Pin_1, IC11.pin1, R158.Pin_0
  N79: R154.Pin_1, IC11.pin14, R159.Pin_0
  N80: IC11.pin2, R157.Pin_1, R158.Pin_1
  N81: IC11.pin6, R155.Pin_1, R160.Pin_0
  N82: IC11.pin13, R156.Pin_0, R159.Pin_1

notes:
  To VGA Monitor
  MIDI Input Jack
  DC Power In
  MIDI Keyboard USB Power
  5 V Power
  Left Side Disabled
  MIDI Isolation Circuit
  VCO Outputs
  MIDI UART Input
  Split Power Supply
  VCOs (3x)
  Summing Amplifier
  Mixer
  Filter
  Speaker

custom parts:
  PmodDA4: Engineered around the Analog Devices AD5628 Digital to Analog Converter, the Digilent PmodDA4 provides 8 channels of D/A conversion at 12 bits of resolution. The PmodDA4 can be used with Digilent system boards as well as a growing number of third-party boards equipped with Digilent Pmod™ connectors. The PmodDA4 can produce an analog output ranging from 0V to 2.5V when operated with a 3.3V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
  YwRobot Breadboard Power Supply: The YwRobot Breadboard Power Supply (MB-V2) has two power rails; they can be 5V or 3V3. Power to the module can be provided through the female USB socket or through the A10 (female) 2.1mm power jack.
  Digilent Basys 3: The Basys 3 board is a complete, ready-to-use digital circuit development platform based on the latest Artix®-7 Field Programmable Gate Array (FPGA) from Xilinx®. With its high-capacity FPGA (Xilinx part number XC7A35T-1CPG236C), low overall cost, and collection of USB, VGA, and other ports, the Basys 3 can host designs ranging from introductory combinational circuits to complex sequential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
